// Digital circuit finalproject.dig as structural Verilog
module finalproject (
  input  VS,
  input  PB,
  input  TR,
  input  EM,
  input  CLK
);

  wire _7448_1_pin1, _7448_1_pin2, _7448_1_pin6, _7448_1_pin7, _7448_1_pin9, _7448_1_pin10, _7448_1_pin11,
       _7448_1_pin12, _7448_1_pin13, _7448_1_pin14, _7448_1_pin15, _7448_2_pin1, _7448_2_pin2, _7448_2_pin6,
       _7448_2_pin7, _7448_2_pin9, _7448_2_pin10, _7448_2_pin11, _7448_2_pin12, _7448_2_pin13, _7448_2_pin14,
       _7448_2_pin15, _7448_3_pin1, _7448_3_pin2, _7448_3_pin6, _7448_3_pin7, _7448_3_pin9, _7448_3_pin10,
       _7448_3_pin11, _7448_3_pin12, _7448_3_pin13, _7448_3_pin14, _7448_3_pin15, _74191_1_pin11,
       _74191_2_pin11, _74191_3_pin11, and_1_out, and_2_out, and_3_out, and_5_out, and_6_out, and_7_out,
       and_8_out, and_9_out, and_10_out, and_11_out, and_12_out, and_13_out, and_14_out, and_15_out,
       DFF_pin5, DFF_pin6, DFF_pin8, DFF_pin9, DFF_pin12, nand_1_out, not_2_out, not_3_out, not_4_out,
       not_5_out, not_6_out, not_7_out, not_8_out, or_1_out, or_2_out, or_4_out, or_5_out;

  _7448 _7448_1 (
    .pin1(_7448_1_pin1), .pin2(_7448_1_pin2), .pin3(1'b1), .pin4(1'b1), .pin5(1'b1), .pin6(_7448_1_pin6),
    .pin7(_7448_1_pin7), .pin8(1'b0), .pin9(_7448_1_pin9), .pin10(_7448_1_pin10), .pin11(_7448_1_pin11),
    .pin12(_7448_1_pin12), .pin13(_7448_1_pin13), .pin14(_7448_1_pin14), .pin15(_7448_1_pin15), .pin16(1'b1));
  _7448 _7448_2 (
    .pin1(_7448_2_pin1), .pin2(_7448_2_pin2), .pin3(1'b1), .pin4(1'b1), .pin5(1'b1), .pin6(_7448_2_pin6),
    .pin7(_7448_2_pin7), .pin8(1'b0), .pin9(_7448_2_pin9), .pin10(_7448_2_pin10), .pin11(_7448_2_pin11),
    .pin12(_7448_2_pin12), .pin13(_7448_2_pin13), .pin14(_7448_2_pin14), .pin15(_7448_2_pin15), .pin16(1'b1));
  _7448 _7448_3 (
    .pin1(_7448_3_pin1), .pin2(_7448_3_pin2), .pin3(1'b1), .pin4(1'b1), .pin5(1'b1), .pin6(_7448_3_pin6),
    .pin7(_7448_3_pin7), .pin8(1'b0), .pin9(_7448_3_pin9), .pin10(_7448_3_pin10), .pin11(_7448_3_pin11),
    .pin12(_7448_3_pin12), .pin13(_7448_3_pin13), .pin14(_7448_3_pin14), .pin15(_7448_3_pin15), .pin16(1'b1));
  Seven_Seg seven_seg_1 (
    .a(_7448_1_pin13), .b(_7448_1_pin12), .c(_7448_1_pin11), .d(_7448_1_pin10), .e(_7448_1_pin9),
    .f(_7448_1_pin15), .g(_7448_1_pin14), .dp(1'b0));
  Seven_Seg seven_seg_2 (
    .a(_7448_2_pin13), .b(_7448_2_pin12), .c(_7448_2_pin11), .d(_7448_2_pin10), .e(_7448_2_pin9),
    .f(_7448_2_pin15), .g(_7448_2_pin14), .dp(1'b0));
  Seven_Seg seven_seg_3 (
    .a(_7448_3_pin13), .b(_7448_3_pin12), .c(_7448_3_pin11), .d(_7448_3_pin10), .e(_7448_3_pin9),
    .f(_7448_3_pin15), .g(_7448_3_pin14), .dp(1'b0));
  _74191 _74191_1 (
    .pin1(1'b0), .pin2(_7448_1_pin1), .pin3(_7448_1_pin7), .pin4(1'b0), .pin5(1'b0), .pin6(_7448_1_pin2),
    .pin7(_7448_1_pin6), .pin8(1'b0), .pin9(1'b0), .pin10(1'b0), .pin11(_74191_1_pin11), .pin14(CLK),
    .pin15(1'b0), .pin16(1'b1));  // open: pin12, pin13
  _74191 _74191_2 (
    .pin1(1'b0), .pin2(_7448_2_pin1), .pin3(_7448_2_pin7), .pin4(1'b0), .pin5(1'b0), .pin6(_7448_2_pin2),
    .pin7(_7448_2_pin6), .pin8(1'b0), .pin9(1'b0), .pin10(1'b0), .pin11(_74191_2_pin11), .pin14(CLK),
    .pin15(1'b0), .pin16(1'b1));  // open: pin12, pin13
  _74191 _74191_3 (
    .pin1(1'b0), .pin2(_7448_3_pin1), .pin3(_7448_3_pin7), .pin4(1'b0), .pin5(1'b0), .pin6(_7448_3_pin2),
    .pin7(_7448_3_pin6), .pin8(1'b0), .pin9(1'b0), .pin10(1'b0), .pin11(_74191_3_pin11), .pin14(CLK),
    .pin15(1'b0), .pin16(1'b1));  // open: pin12, pin13
  not not_1 (_74191_1_pin11, and_2_out);
  xor xor_1 (_74191_3_pin11, and_1_out, 1'b1);
  and and_1 (and_1_out, _7448_3_pin7, and_3_out);
  and and_2 (and_2_out, _7448_1_pin1, _7448_1_pin7);
  and and_3 (and_3_out, _7448_3_pin7, _7448_3_pin1, _7448_3_pin2);
  and and_4 (_74191_2_pin11, or_1_out, and_5_out);
  not not_2 (not_2_out, _7448_2_pin6);
  and and_5 (and_5_out, DFF_pin6, DFF_pin8);
  not not_3 (not_3_out, TR);
  not not_4 (not_4_out, EM);
  or or_1 (or_1_out, VS, PB);
  not not_5 (not_5_out, and_2_out);
  not not_6 (not_6_out, not_2_out);
  nand nand_1 (nand_1_out, not_3_out, and_3_out, and_8_out);
  not not_7 (not_7_out, and_3_out);
  and and_6 (and_6_out, not_5_out, not_4_out, DFF_pin5, DFF_pin8);
  and and_7 (and_7_out, not_4_out, not_6_out, not_3_out, DFF_pin8, DFF_pin6);
  and and_8 (and_8_out, DFF_pin9, DFF_pin6);
  and and_9 (and_9_out, and_8_out, nand_1_out, not_7_out);
  and and_10 (and_10_out, DFF_pin9, and_2_out, DFF_pin5);
  and and_11 (and_11_out, DFF_pin5, and_2_out, DFF_pin8);
  // Probe on and_11_out
  or or_2 (or_2_out, and_10_out, and_11_out, and_9_out, and_7_out);
  _7474 DFF (
    .pin1(1'b1), .pin2(or_2_out), .pin3(CLK), .pin4(1'b1), .pin5(DFF_pin5), .pin6(DFF_pin6), .pin7(1'b0),
    .pin8(DFF_pin8), .pin9(DFF_pin9), .pin10(1'b1), .pin11(CLK), .pin12(DFF_pin12), .pin13(1'b1), .pin14(1'b1));
  or or_3 (DFF_pin12, and_10_out, and_6_out, and_9_out);
  and and_12 (and_12_out, DFF_pin5, DFF_pin9);
  and and_13 (and_13_out, DFF_pin9, DFF_pin6);
  and and_14 (and_14_out, DFF_pin8, not_4_out, DFF_pin6);
  and and_15 (and_15_out, DFF_pin8, DFF_pin5);
  not not_8 (not_8_out, not_4_out);
  or or_4 (or_4_out, and_12_out, not_8_out, and_13_out);
  or or_5 (or_5_out, and_14_out, not_8_out, and_15_out);
  LED led_1 (.in(and_14_out));
  LED led_2 (.in(and_15_out));
  LED led_3 (.in(or_4_out));
  LED led_4 (.in(and_13_out));
  LED led_5 (.in(and_12_out));
  LED led_6 (.in(or_5_out));

  // Notes on the sheet:
  //   TS
  //   TY
  //   TL
  //   Stay at 10
  //   Go from 01 -> 10
  //   Check 1Q and 2Q*
  //   to make sure we 
  //   are first in 01.
  //   Use 1Q* and 2Q* to check 
  //   we are in 00 before going to 01
  //   In State 10
  //   Go from 00 -> 01
  //   Stay at 11
  //   Stay at 01
  //   1D OR Gate
  //   2D OR gate
  //   1Q = S0 = LSB
  //   2Q = S1 = MSB
  //   2RD, 2SD, 1SD, 1RD to VCC 
  //   so that it doesn't set/reset
  //   Check EM not active for Green (00)
  //   Main
  //   Side
endmodule
